// Logisim project 1 MUX.circ as structural Verilog
module _2_1_MUX (
  input  in_0,
  input  in_1,
  input  select,
  output out_4
);

  wire and_1_out, and_2_out, not_1_out, undriven;

  and and_1 (and_1_out, in_0, not_1_out);
  not not_1 (not_1_out, undriven);
  and and_2 (and_2_out, in_1, undriven);
  or or_1 (out_4, and_1_out, and_2_out);

  // Notes on the sheet:
  //   Something is wrong
endmodule

module _4_1_MUX (
  input  in_1,
  input  in_2,
  input  in_3,
  input  in_4,
  input  in_5,
  input  in_6,
  output out_7
);

  wire n2_1_mux_1_out_4, n2_1_mux_2_out_4;

  _2_1_MUX u_2_1_mux_1 (.in_1(in_1), .select(in_2), .out_4(n2_1_mux_1_out_4));  // open: in_0
  _2_1_MUX u_2_1_mux_2 (.in_1(in_3), .select(in_4), .out_4(n2_1_mux_2_out_4));  // open: in_0
  // _2_1_MUX 2_1_mux_3: pin names not known; wires that end beside it: n2_1_mux_1_out_4, n2_1_mux_2_out_4, out_7
endmodule
