// Logisim project Cache.circ as structural Verilog: 10 circuits, main circuit main
module main (
  input  EnableTestHalting,
  output [9:0] CorrectCounter,
  output [9:0] HitCounter,
  output [9:0] MissCounter,
  output [9:0] TestNumber,
  output [7:0] ByteRead,
  output [7:0] CorrectByteRead,
  output Halt
);

  wire and_3_out, and_4_out, and_5_out, CLK, CmdIsRead, Correct, CpuRead, CpuWrite, DidContain, HaltTesting,
       MaxItersReached, MemRead, MemWrite, not_1_out, not_2_out, not_4_out, NotDoneTesting, Ok2Count,
       or_1_out, Ready;
  wire [7:0] CpuWriteValue, MemAddress;
  wire [9:0] CpuAddress;
  wire [31:0] Line2Mem, LineFromMem;

  not not_1 (not_1_out, Ready);
  Clock clock_1 (.out(CLK));
  or or_1 (or_1_out, MaxItersReached, Ready);
  Counter #(.width(4), .max('h9)) MaxClocks (
    .load(Ready), .D(4'b0001), .count(not_1_out), .carry(MaxItersReached), .clk(CLK));  // open: Q, clr
  and and_1 (HaltTesting, EnableTestHalting, CmdIsRead, not_2_out);
  not not_2 (not_2_out, Correct);
  not not_3 (NotDoneTesting, Halt);
  Inputs inputs_1 (
    .HaltTesting(HaltTesting), .Ready(or_1_out), .CLK(CLK), .Done(Halt), .Read(CpuRead), .Write(CpuWrite),
    .Address(CpuAddress), .Value(CpuWriteValue), .TestNumber(TestNumber));
  Cache cache_1 (
    .CpuAddress(CpuAddress), .CpuRead(CpuRead), .CpuWrite(CpuWrite), .CpuWriteValue(CpuWriteValue),
    .CLK(CLK), .Ready(Ready), .DidContain(DidContain), .ByteRead(ByteRead), .MemAddress(MemAddress),
    .MemRead(MemRead), .MemWrite(MemWrite), .LineFromMem(LineFromMem), .Line2Mem(Line2Mem));
  // Probe on CpuRead
  // Probe on CpuWrite
  // Probe on CpuAddress
  // Probe on CpuWriteValue
  // Probe on TestNumber
  // Probe on CorrectByteRead
  // Probe on Correct
  // Probe on Ready
  // Probe on DidContain
  // Probe on ByteRead
  // Probe on MemAddress
  // Probe on MemRead
  // Probe on MemWrite
  // Probe on HitCounter
  // Probe on LineFromMem
  // Probe on Line2Mem
  not not_4 (not_4_out, HaltTesting);
  RAM #(.dataWidth(32), .bus("separate")) ram_1 (
    .addr(MemAddress), .din(Line2Mem), .data(LineFromMem), .str(MemWrite), .clk(CLK), .ld(MemRead));  // open: sel, clr
  and and_2 (Ok2Count, Ready, not_4_out, NotDoneTesting);
  and and_3 (and_3_out, Correct, Ok2Count);
  and and_4 (and_4_out, DidContain, Ok2Count);
  and and_5 (and_5_out, MemRead, NotDoneTesting);
  Checker checker_1 (
    .TestNumber(TestNumber), .YourByteRead(ByteRead), .CmdIsRead(CmdIsRead),
    .CorrectByteRead(CorrectByteRead), .Correct(Correct));
  Counter #(.width(10), .max('h3ff)) u_CorrectCounter (
    .count(and_3_out), .Q(CorrectCounter), .clk(CLK));  // open: load, D, carry, clr
  Counter #(.width(10), .max('h3ff)) u_HitCounter (
    .count(and_4_out), .Q(HitCounter), .clk(CLK));  // open: load, D, carry, clr
  Counter #(.width(10), .max('h3ff)) u_MissCounter (
    .count(and_5_out), .Q(MissCounter), .clk(CLK));  // open: load, D, carry, clr
  // Probe on CorrectCounter
  // Probe on HitCounter
  // Probe on MissCounter

  // Other names for the same wires on the sheet: DoneTesting = Halt

  // Notes on the sheet:
  //   Your Answer Inside Here
  //   Claudia Chen: 913175637
  //   Armand Nasseri: 912679383
endmodule

module Cache (
  input  [9:0] CpuAddress,
  input  CpuRead,
  input  CpuWrite,
  input  [7:0] CpuWriteValue,
  input  CLK,
  input  [31:0] LineFromMem,
  output Ready,
  output DidContain,
  output [7:0] ByteRead,
  output [7:0] MemAddress,
  output MemRead,
  output MemWrite,
  output [31:0] Line2Mem
);

  wire and_1_out, and_2_out, and_3_out, contains, CpuRead_t, CpuWrite_t, Dirty0, Dirty1, Evict0, Evict1,
       GotoSet1, GotoSet2, Isdirty, lol, MemRead_t, MemWritee, miss0, miss1, not_1_out, not_2_out, not_3_out,
       update_Ages;
  wire [2:0] fsm_controller_1_s0, init;
  wire [6:0] Tag_Out1, Tag_Out2;
  wire [7:0] ByteOut_A, ByteOut_B, CpuWriteValue_t, newMemAddress;
  wire [9:0] CpuAddress_t;
  wire [31:0] LineFromMemA, LineFromMemB;

  Register #(.width(10)) State (.D(CpuAddress), .en(Ready), .Q(CpuAddress_t), .clk(CLK));  // open: clr
  Register #(.width(1)) State_2 (.D(CpuRead), .en(Ready), .Q(CpuRead_t), .clk(CLK));  // open: clr
  Register #(.width(1)) State_3 (.D(CpuWrite), .en(Ready), .Q(CpuWrite_t), .clk(CLK));  // open: clr
  Register State_4 (.D(CpuWriteValue), .en(Ready), .Q(CpuWriteValue_t), .clk(CLK));  // open: clr
  not not_1 (not_1_out, miss0);
  and and_1 (and_1_out, not_1_out, GotoSet1);
  not not_2 (not_2_out, miss1);
  and and_2 (and_2_out, not_2_out, GotoSet2);
  fsm__controller fsm_controller_1 (
    .c2(init[2]), .c1(init[1]), .c0(init[0]), .read(CpuRead_t), .write(CpuWrite_t), .contain(contains),
    .dirty(1'b0), .s2(fsm_controller_1_s0[2]), .s1(fsm_controller_1_s0[1]), .s0(fsm_controller_1_s0[0]),
    .ready(Ready), .memRead(MemRead_t), .memWrite(MemWritee), .updateAge(update_Ages), .readddddd(lol));
  Register #(.width(3)) State_5 (.D(fsm_controller_1_s0), .Q(init), .clk(CLK));  // open: en, clr
  Multiplexer #(.enable("false")) multiplexer_1 (.in0(Dirty0), .in1(Dirty1), .out(Isdirty), .sel(CpuAddress_t[2]));
  or or_1 (contains, and_1_out, and_2_out);
  Demultiplexer #(.enable("false")) demultiplexer_1 (
    .out0(GotoSet1), .out1(GotoSet2), .in(1'b1), .sel(CpuAddress_t[2]));
  Set0 set0_1 (
    .TAG(CpuAddress_t[9:3]), .CLK(CLK), .inSet(GotoSet1), .Offset(CpuAddress_t[1:0]), .Init(init),
    .MemRead(MemRead_t), .MemWrite(MemWritee), .Update_Ages(update_Ages), .CPUWriteValue(CpuWriteValue_t),
    .LineFromMem(LineFromMem), .miss(miss0), .Dirty(Dirty0), .Evict(Evict0), .Tag_2(Tag_Out1),
    .ByteOut(ByteOut_A), .Line2Men(LineFromMemA));  // open: CLK_2, CLK_3, CLK_4, CLK_5, CLK_6, CLK_7, SetAge0, SetAge0_2, SetAge0_3, SetAge0_4, SetAge0_5, SetAge0_6, SetAge0_7
  Set0 set0_2 (
    .TAG(CpuAddress_t[9:3]), .CLK(CLK), .inSet(GotoSet2), .Offset(CpuAddress_t[1:0]), .Init(init),
    .MemRead(MemRead_t), .MemWrite(MemWritee), .Update_Ages(update_Ages), .CPUWriteValue(CpuWriteValue_t),
    .LineFromMem(LineFromMem), .miss(miss1), .Dirty(Dirty1), .Evict(Evict1), .Tag_2(Tag_Out2),
    .ByteOut(ByteOut_B), .Line2Men(LineFromMemB));  // open: CLK_2, CLK_3, CLK_4, CLK_5, CLK_6, CLK_7, SetAge0, SetAge0_2, SetAge0_3, SetAge0_4, SetAge0_5, SetAge0_6, SetAge0_7
  Multiplexer #(.width(8), .enable("false")) multiplexer_2 (
    .in0(ByteOut_A), .in1(ByteOut_B), .out(ByteRead), .sel(CpuAddress_t[2]));
  and and_3 (and_3_out, lol, contains);
  Multiplexer #(.width(8), .enable("false")) multiplexer_3 (
    .in0({Tag_Out1, CpuAddress_t[2]}), .in1({Tag_Out2, CpuAddress_t[2]}), .out(newMemAddress),
    .sel(CpuAddress_t[2]));
  Register #(.width(1), .trigger("high")) State_6 (.D(and_3_out), .Q(DidContain), .clk(lol));  // open: en, clr
  Multiplexer #(.width(32), .enable("false")) multiplexer_4 (
    .in0(LineFromMemA), .in1(LineFromMemB), .out(Line2Mem), .sel(CpuAddress_t[2]));
  Multiplexer #(.width(8), .enable("false")) multiplexer_5 (
    .in0(CpuAddress_t[9:2]), .in1(newMemAddress), .out(MemAddress), .sel(MemWrite));
  and and_4 (MemRead, MemRead_t, not_3_out);
  not not_3 (not_3_out, contains);
  or or_2 (MemWrite, Evict0, Evict1);

  // Other names for the same wires on the sheet: SET = CpuAddress_t[2]; Set_t = CpuAddress_t[2];
  //   OFFSET[1:0] = CpuAddress_t[1:0]; Offset_t[1:0] = CpuAddress_t[1:0]; TAG[6:0] = CpuAddress_t[9:3];
  //   Tag_t[6:0] = CpuAddress_t[9:3]; MemWrite2 = MemWrite

  // Notes on the sheet:
  //   Address Bits = 10
  //   Line Size = 4
  //   W = 3
  //   Num Sets = 2
  //   C =4*3*2 = 24bytes
  //   Tag bits = 7
  //   INPUTS ON THE RIGHT
endmodule

module Inputs (
  input  HaltTesting,
  input  Ready,
  input  CLK,
  output Done,
  output Read,
  output Write,
  output [9:0] Address,
  output [7:0] Value,
  output [9:0] TestNumber
);

  wire and_1_out, not_1_out, not_2_out;

  not not_1 (not_1_out, HaltTesting);
  not not_2 (not_2_out, Done);
  Counter #(.width(10), .max('h3ff), .ongoal("stay")) u_TestNumber (
    .count(and_1_out), .Q(TestNumber), .clk(CLK));  // open: load, D, carry, clr
  and and_1 (and_1_out, not_1_out, Ready, not_2_out);
  ROM #(.addrWidth(10), .dataWidth(21)) rom_1 (
    .addr(TestNumber), .data({Done, Read, Write, Address, Value}));  // open: sel

  // Notes on the sheet:
  //   contents of rom_1 (hex, n*v repeats v):
  //   80882 83fe6 4306b 83e0e 43701 42275 8280f 80304 41bd8 84371 43f77 41d70 4250b 44733 8253d 440d8
  //   82691 440c9 83d7c 43558 446bf 83837 842c9 43e0f 4059d 41556 80166 833b0 43a89 83142 8361c 42e66
  //   43eb6 42c00 43a0e 8165c 84682 8092a 83907 41f89 817b0 40855 82056 425e8 43ff2 8039f 42bd7 82137
  //   4416b 40273 8324a 814e4 44570 41c0f 429da 82640 8069c 8099e 414d5 41004 81beb 84113 419b1 81add
  //   83f35 425ff 829cd 40250 82945 4366d 40cc2 444f8 80814 81156 8446d 42a82 42bae 82578 41135 405d0
  //   8304b 82b3a 40972 822ba 4443a 42337 82506 80bd3 80560 83552 83955 81434 43096 43da1 81aa2 80305
  //   428e6 428cc 808a2 40e80 845f0 4215d 82765 82e29 40be5 82b74 42715 417a2 41fab 8452f 81c0a 83325
  //   44624 80205 42dfc 41333 40958 81348 42736 41069 84510 44669 826dd 8067e 408e4 44680 444e8 832ad
  //   821f8 83509 82d46 81184 432cd 80b77 4005a 440e0 81ea0 43d73 42b8c 80624 41468 42699 415ed 80fc1 0
  //   100000
endmodule

module Checker (
  input  [9:0] TestNumber,
  input  [7:0] YourByteRead,
  output CmdIsRead,
  output [7:0] CorrectByteRead,
  output Correct
);

  wire comparator_1_eq;
  wire [9:0] subtractor_1_out;

  // Probe on TestNumber
  Subtractor #(.width(10)) subtractor_1 (.a(TestNumber), .b(10'h1), .out(subtractor_1_out));  // open: bin, bout
  ROM #(.addrWidth(10), .dataWidth(9)) rom_1 (
    .addr(subtractor_1_out), .data({CmdIsRead, CorrectByteRead}));  // open: sel
  Comparator #(.mode("unsigned")) comparator_1 (
    .a(YourByteRead), .b(CorrectByteRead), .eq(comparator_1_eq));  // open: gt, lt
  and and_1 (Correct, comparator_1_eq, CmdIsRead);

  // Other names for the same wires on the sheet: Test_Number[9:0] = TestNumber

  // Notes on the sheet:
  //   Read Solutions
  //   contents of rom_1 (hex, n*v repeats v):
  //   1a3 1dc 6b 125 1 75 1dc 1c3 d8 1ab 77 70 b 33 10b d8 1c3 c9 174 58 bf 153 199 f 9d 56 1bb 13b 89 16c
  //   180 66 b6 0 e 107 1bf 1d8 167 89 118 55 1a2 e8 f2 1c3 d7 142 6b 73 1ab 18c 70 f da 1c3 14c 1d8 d5 4
  //   1d8 16b b1 1f4 1f2 ff 1da 50 1da 6d c2 f8 155 1c6 1f8 82 ae 1ff 35 d0 16b 1ae 72 175 3a 37 1ff 173
  //   1d0 158 167 1d5 96 a1 1f4 1c3 e6 cc 155 80 170 5d 1e6 166 e5 1ae 15 a2 ab 170 10f 13b 24 150 fc 33
  //   58 133 36 69 170 69 1c3 14c e4 80 e8 1ab 15d 158 1fc 135 cd 1e5 5a e0 104 73 8c 14c 68 99 ed 1a6
endmodule

module Set0 (
  input  [6:0] TAG,
  input  CLK,
  input  inSet,
  input  [1:0] Offset,
  input  [2:0] Init,
  input  MemRead,
  input  MemWrite,
  input  CLK_2,
  input  CLK_3,
  input  CLK_4,
  input  Update_Ages,
  input  CLK_5,
  input  CLK_6,
  input  CLK_7,
  input  [7:0] CPUWriteValue,
  input  [31:0] LineFromMem,
  output miss,
  output Dirty,
  output Evict,
  output SetAge0,
  output SetAge0_2,
  output SetAge0_3,
  output SetAge0_4,
  output SetAge0_5,
  output SetAge0_6,
  output SetAge0_7,
  output [6:0] Tag_2,
  output [7:0] ByteOut,
  output [31:0] Line2Men
);

  wire Accesssed_1, Accesssed_2, Accesssed_3, and_1_out, and_2_out, and_3_out, and_4_out, and_5_out,
       and_8_out, and_9_out, and_10_out, and_11_out, and_12_out, and_13_out, and_14_out, and_15_out,
       and_16_out, and_17_out, and_18_out, and_19_out, and_20_out, Dirty0, Dirty0_In, Dirty0_q, Dirty1,
       Dirty1_in, Dirty1_q, Dirty2, Dirty2_in, Dirty2_q, Evict0, Evict1, Evict2, GoToBlock1, GoToBlock2,
       GoToBlock3, hit0, hit1, hit2, InitalizeAge, multiplexer_2_out, not_1_out, not_2_out, not_3_out,
       not_4_out, not_5_out, not_6_out, notDirty, or_1_out, or_2_out, or_3_out, or_4_out, or_5_out, or_6_out,
       or_7_out, V0, V0_In, V1, V1_In, V2, V2_in;
  wire [1:0] Accesssed, Age0, Age1, Age2, Biggest_Age, Biggest_Boi, multiplexer_1_out, multiplexer_3_out,
       multiplexer_4_out, multiplexer_5_out, multiplexer_6_out, multiplexer_7_out, multiplexer_9_out,
       multiplexer_11_out, multiplexer_12_out, New_Age1, New_Age2, New_Age3, WriteTo;
  wire [6:0] Tag0, Tag0_In, Tag1, Tag1_In, Tag2, Tag2_In, Tag_1, Tag_2_t, Tag_3;
  wire [7:0] Byte_Read0, Byte_Read1, Byte_Read2;
  wire [31:0] Data0, Data0_In, Data1, Data1_in, Data2, Data2_in, Line_Out_0, Line_Out_1, Line_Out_2;

  Comparator #(.width(3), .mode("unsigned")) comparator_1 (.a(Init), .b(3'b000), .eq(InitalizeAge));  // open: gt, lt
  and and_1 (and_1_out, Update_Ages, inSet);
  buf and_2 (and_2_out, inSet);  // AND_Gate
  BigBois bigbois_1 (
    .Age_0(Age0), .Age_1(Age1), .Age_2(Age2), .BIGBOI(Biggest_Boi), .A1(Accesssed_1), .A2(Accesssed_2),
    .A3(Accesssed_3), .New_Age0(New_Age1), .New_Age1(New_Age2), .New_Age2(New_Age3));
  buf and_3 (and_3_out, inSet);  // AND_Gate
  buf and_4 (and_4_out, inSet);  // AND_Gate
  buf and_5 (and_5_out, inSet);  // AND_Gate
  Multiplexer #(.width(2), .enable("false")) multiplexer_1 (
    .in0(New_Age1), .in1(2'b00), .out(multiplexer_1_out), .sel(InitalizeAge));
  or or_1 (or_1_out, and_1_out, InitalizeAge);
  // Probe on Age0
  Register #(.width(2)) u_Age0 (.D(multiplexer_1_out), .en(or_1_out), .Q(Age0), .clk(CLK));  // open: clr
  // Probe on Data0
  Register #(.width(32)) u_Data0 (.D(Data0_In), .en(and_2_out), .Q(Data0), .clk(CLK));  // open: clr
  // Probe on Tag0
  Register #(.width(7)) u_Tag0 (.D(Tag0_In), .en(and_3_out), .Q(Tag0), .clk(CLK));  // open: clr
  // Probe on V0
  Register #(.width(1)) u_V0 (.D(V0_In), .en(and_4_out), .Q(V0), .clk(CLK));  // open: clr
  // Probe on Dirty0_q
  Register #(.width(1)) u_Dirty0 (.D(Dirty0_In), .en(and_5_out), .Q(Dirty0_q), .clk(CLK));  // open: clr
  HowOldAmI howoldami_1 (.Age_1(Age0), .Age_2(Age1), .Age_3(Age2), .Grandpa(Biggest_Age), .BiggestBoi(Biggest_Boi));
  Multiplexer #(.enable("false")) multiplexer_2 (.in0(1'b0), .in1(1'b1), .out(multiplexer_2_out), .sel(or_2_out));
  or or_2 (or_2_out, MemRead, MemWrite);
  not not_1 (not_1_out, hit0);
  not not_2 (not_2_out, hit1);
  not not_3 (not_3_out, hit2);
  not not_4 (not_4_out, Dirty0);
  not not_5 (not_5_out, Dirty1);
  not not_6 (not_6_out, Dirty2);
  // Probe on Biggest_Age
  Demultiplexer #(.select(2), .enable("false")) demultiplexer_1 (
    .out0(GoToBlock1), .out1(GoToBlock2), .out2(GoToBlock3), .in(multiplexer_2_out), .sel(multiplexer_4_out));  // open: out3
  Multiplexer #(.width(2), .enable("false")) multiplexer_3 (
    .in0(2'b00), .in1(WriteTo), .out(multiplexer_3_out), .sel(MemWrite));
  and and_6 (notDirty, not_4_out, not_5_out, not_6_out);
  Multiplexer #(.width(2), .enable("false")) multiplexer_4 (
    .in0(multiplexer_3_out), .in1(Biggest_Age), .out(multiplexer_4_out), .sel(MemRead));
  and and_7 (miss, not_1_out, not_2_out, not_3_out);
  buf and_8 (and_8_out, inSet);  // AND_Gate
  buf and_9 (and_9_out, inSet);  // AND_Gate
  buf and_10 (and_10_out, inSet);  // AND_Gate
  Multiplexer #(.width(2), .enable("false")) multiplexer_5 (
    .in0(New_Age2), .in1(2'b01), .out(multiplexer_5_out), .sel(InitalizeAge));
  buf and_11 (and_11_out, inSet);  // AND_Gate
  // Probe on Tag1
  Register #(.width(7)) u_Tag1 (.D(Tag1_In), .en(and_8_out), .Q(Tag1), .clk(CLK));  // open: clr
  // Probe on V1
  Register #(.width(1)) u_V1 (.D(V1_In), .en(and_9_out), .Q(V1), .clk(CLK));  // open: clr
  and and_12 (and_12_out, Update_Ages, inSet);
  or or_3 (or_3_out, and_12_out, InitalizeAge);
  Register #(.width(32)) u_Data1 (.D(Data1_in), .en(and_11_out), .Q(Data1), .clk(CLK));  // open: clr
  // Probe on Dirty1_q
  Register #(.width(1)) u_Dirty1 (.D(Dirty1_in), .en(and_10_out), .Q(Dirty1_q), .clk(CLK));  // open: clr
  // Probe on Age1
  Register #(.width(2)) u_Age1 (.D(multiplexer_5_out), .en(or_3_out), .Q(Age1), .clk(CLK));  // open: clr
  // Probe on Data1
  buf and_13 (and_13_out, inSet);  // AND_Gate
  buf and_14 (and_14_out, inSet);  // AND_Gate
  buf and_15 (and_15_out, inSet);  // AND_Gate
  Multiplexer #(.width(2), .enable("false")) multiplexer_6 (
    .in0(New_Age3), .in1(2'b10), .out(multiplexer_6_out), .sel(InitalizeAge));
  and and_16 (and_16_out, Update_Ages, inSet);
  buf and_17 (and_17_out, inSet);  // AND_Gate
  and and_18 (and_18_out, inSet, MemRead);
  or or_4 (or_4_out, GoToBlock3, hit2);
  // Probe on Tag2
  Register #(.width(7)) u_Tag2 (.D(Tag2_In), .en(and_13_out), .Q(Tag2), .clk(CLK));  // open: clr
  Register #(.width(1)) u_V2 (.D(V2_in), .en(and_14_out), .Q(V2), .clk(CLK));  // open: clr
  // Probe on Age2
  Register #(.width(2)) u_Age2 (.D(multiplexer_6_out), .en(or_5_out), .Q(Age2), .clk(CLK));  // open: clr
  or or_5 (or_5_out, and_16_out, InitalizeAge);
  block block_1 (
    .CpuWriteValue(CPUWriteValue), .MemWrite(MemWrite), .TAG(TAG), .CLK(CLK), .Read(MemRead), .OS(Offset),
    .Inblock(GoToBlock1), .InSet(inSet), .MemRead(LineFromMem), .Hit(hit0), .DirtyBit(Dirty0),
    .Evict(Evict0), .Tag_Out(Tag_1), .ByteRead(Byte_Read0), .LineFromCache(Line_Out_0));  // open: CpuRead, dirty, SetAge0, SetAge0_2, SetAge0_3, SetAge0_4, SetAge0_5, SetAge0_6, SetAge0_7, SetAge0_8, SetAge0_9, SetAge0_10, SetAge0_11
  block block_2 (
    .CpuWriteValue(CPUWriteValue), .MemWrite(MemWrite), .TAG(TAG), .CLK(CLK), .Read(MemRead), .OS(Offset),
    .Inblock(GoToBlock2), .InSet(inSet), .MemRead(LineFromMem), .Hit(hit1), .DirtyBit(Dirty1),
    .Evict(Evict1), .Tag_Out(Tag_2_t), .ByteRead(Byte_Read1), .LineFromCache(Line_Out_1));  // open: CpuRead, dirty, SetAge0, SetAge0_2, SetAge0_3, SetAge0_4, SetAge0_5, SetAge0_6, SetAge0_7, SetAge0_8, SetAge0_9, SetAge0_10, SetAge0_11
  D_Flip_Flop #(.trigger("high")) d_ff_1 (
    .clk(and_18_out), .D(or_4_out), .Q(Accesssed_3));  // open: Qn, preset, en, reset
  block block_3 (
    .CpuWriteValue(CPUWriteValue), .MemWrite(MemWrite), .TAG(TAG), .CLK(CLK), .Read(MemRead), .OS(Offset),
    .Inblock(GoToBlock3), .InSet(inSet), .MemRead(LineFromMem), .Hit(hit2), .DirtyBit(Dirty2),
    .Evict(Evict2), .Tag_Out(Tag_3), .ByteRead(Byte_Read2), .LineFromCache(Line_Out_2));  // open: CpuRead, dirty, SetAge0, SetAge0_2, SetAge0_3, SetAge0_4, SetAge0_5, SetAge0_6, SetAge0_7, SetAge0_8, SetAge0_9, SetAge0_10, SetAge0_11
  // Probe on V2
  // Probe on Dirty2_q
  Register #(.width(1)) u_Dirty2 (.D(Dirty2_in), .en(and_15_out), .Q(Dirty2_q), .clk(CLK));  // open: clr
  Register #(.width(32)) u_Data2 (.D(Data2_in), .en(and_17_out), .Q(Data2), .clk(CLK));  // open: clr
  and and_19 (and_19_out, MemRead, inSet);
  or or_6 (or_6_out, GoToBlock2, hit1);
  // Probe on Data2
  D_Flip_Flop #(.trigger("high")) d_ff_2 (
    .clk(and_19_out), .D(or_6_out), .Q(Accesssed_2));  // open: Qn, preset, en, reset
  and and_20 (and_20_out, MemRead, inSet);
  or or_7 (or_7_out, GoToBlock1, hit0);
  D_Flip_Flop #(.trigger("high")) d_ff_3 (
    .clk(and_20_out), .D(or_7_out), .Q(Accesssed_1));  // open: Qn, preset, en, reset
  Multiplexer #(.width(2), .enable("false")) multiplexer_7 (
    .in0(2'b00), .in1(2'b00), .out(multiplexer_7_out), .sel(Accesssed_1));
  Multiplexer #(.select(2), .width(8), .enable("false")) multiplexer_8 (
    .in0(Byte_Read0), .in1(Byte_Read1), .in2(Byte_Read2), .out(ByteOut), .sel(Accesssed));  // open: in3
  Multiplexer #(.width(2), .enable("false")) multiplexer_9 (
    .in0(2'b00), .in1(2'b00), .out(multiplexer_9_out), .sel(hit0));
  Multiplexer #(.select(2), .width(32), .enable("false")) multiplexer_10 (
    .in0(Line_Out_0), .in1(Line_Out_1), .in2(Line_Out_2), .out(Line2Men), .sel(Accesssed));  // open: in3
  Multiplexer #(.width(2), .enable("false")) multiplexer_11 (
    .in0(multiplexer_9_out), .in1(2'b01), .out(multiplexer_11_out), .sel(hit1));
  Multiplexer #(.width(2), .enable("false")) multiplexer_12 (
    .in0(multiplexer_7_out), .in1(2'b01), .out(multiplexer_12_out), .sel(Accesssed_2));
  Multiplexer #(.width(2), .enable("false")) multiplexer_13 (
    .in0(multiplexer_11_out), .in1(2'b10), .out(WriteTo), .sel(hit2));
  Multiplexer #(.width(2), .enable("false")) multiplexer_14 (
    .in0(multiplexer_12_out), .in1(2'b10), .out(Accesssed), .sel(Accesssed_3));
  Multiplexer #(.select(2), .enable("false")) multiplexer_15 (
    .in0(Evict0), .in1(Evict1), .in2(Evict2), .out(Evict), .sel(Accesssed));  // open: in3
  not not_7 (Dirty, notDirty);
  Multiplexer #(.select(2), .width(7), .enable("false")) multiplexer_16 (
    .in0(Tag_1), .in1(Tag_2_t), .in2(Tag_3), .out(Tag_2), .sel(Accesssed));  // open: in3

  // Other names for the same wires on the sheet: InSet1 = inSet; OS[1:0] = Offset; Read_Mem = MemRead
endmodule

module Set1 (
  input  [6:0] TAG,
  input  CLK
);

  wire comparator_1_eq, comparator_2_eq, comparator_3_eq, Dirty0, Dirty0_In, Dirty1, Dirty1_in, Dirty2,
       Dirty2_in, Hit, Hit0, Hit1, Hit2, V0, V0_In, V1, V1_In, V2, V2_in, Write_Age0, Write_Age1, Write_Age2,
       Write_Dirty0, Write_Dirty1, Write_Dirty2, Write_Tag0, Write_Tag1, Write_Tag2, Write_V0, Write_V1,
       Write_V2;
  wire [1:0] Age0, Age0_In, Age1, Age1_in, Age2, Age2_in;
  wire [6:0] Tag0, Tag0_In, Tag1, Tag1_In, Tag2, Tag2_In, undriven;
  wire [31:0] Data0, Data0_In, Data1, Data1_in, Data2, Data2_in;

  Comparator #(.width(7), .mode("unsigned")) comparator_1 (.a(TAG), .b(Tag0), .eq(comparator_1_eq));  // open: gt, lt
  Comparator #(.width(7), .mode("unsigned")) comparator_2 (.a(TAG), .b(Tag1), .eq(comparator_2_eq));  // open: gt, lt
  Comparator #(.width(7), .mode("unsigned")) comparator_3 (.a(TAG), .b(Tag2), .eq(comparator_3_eq));  // open: gt, lt
  and and_1 (Hit0, comparator_1_eq, V0);
  and and_2 (Hit1, comparator_2_eq, V1);
  and and_3 (Hit2, comparator_3_eq, V2);
  // Probe on Tag0
  Register #(.width(7)) u_Tag0 (.D(Tag0_In), .en(Write_Tag0), .Q(Tag0), .clk(CLK));  // open: clr
  // Probe on V0
  Register #(.width(1)) u_V0 (.D(V0_In), .en(Write_V0), .Q(V0), .clk(CLK));  // open: clr
  // Probe on Dirty0
  Register #(.width(1)) u_Dirty0 (.D(Dirty0_In), .en(Write_Dirty0), .Q(Dirty0), .clk(CLK));  // open: clr
  // Probe on Age0
  Register #(.width(2)) u_Age0 (.D(Age0_In), .en(Write_Age0), .Q(Age0), .clk(CLK));  // open: clr
  Register #(.width(32)) u_Data0 (.D(Data0_In), .en(Write_Dirty0), .Q(Data0), .clk(CLK));  // open: clr
  // Probe on Data0
  // Probe on Tag1
  Register #(.width(7)) u_Tag1 (.D(Tag1_In), .en(Write_Tag1), .Q(Tag1), .clk(CLK));  // open: clr
  // Probe on V1
  Register #(.width(1)) u_V1 (.D(V1_In), .en(Write_V1), .Q(V1), .clk(CLK));  // open: clr
  // Probe on Dirty1
  Register #(.width(1)) u_Dirty1 (.D(Dirty1_in), .en(Write_Dirty1), .Q(Dirty1), .clk(CLK));  // open: clr
  // Probe on Age1
  Register #(.width(2)) u_Age1 (.D(Age1_in), .en(Write_Age1), .Q(Age1), .clk(CLK));  // open: clr
  Register #(.width(32)) u_Data1 (.D(Data1_in), .en(Write_Dirty1), .Q(Data1), .clk(CLK));  // open: clr
  or or_1 (Hit, Hit0, Hit1, Hit2);
  // Probe on Data1
  // Probe on Tag2
  Register #(.width(7)) u_Tag2 (.D(Tag2_In), .en(Write_Tag2), .Q(Tag2), .clk(CLK));  // open: clr
  // Probe on V2
  Register #(.width(1)) u_V2 (.D(V2_in), .en(Write_V2), .Q(V2), .clk(CLK));  // open: clr
  // Probe on Dirty2
  Register #(.width(1)) u_Dirty2 (.D(Dirty2_in), .en(Write_Dirty2), .Q(Dirty2), .clk(CLK));  // open: clr
  // Probe on Age2
  Register #(.width(2)) u_Age2 (.D(Age2_in), .en(Write_Age2), .Q(Age2), .clk(CLK));  // open: clr
  Register #(.width(32)) u_Data2 (.D(Data2_in), .en(Write_Dirty2), .Q(Data2), .clk(CLK));  // open: clr
  Multiplexer #(.width(7), .enable("false")) multiplexer_1 (.in0(undriven), .sel(Hit));  // open: in1, out
  Demultiplexer #(.enable("false")) demultiplexer_1 ();  // open: out0, out1, in, sel
  // Probe on Data2
endmodule

module fsm__controller (
  input  c2,
  input  c1,
  input  c0,
  input  read,
  input  write,
  input  contain,
  input  dirty,
  output s2,
  output s1,
  output s0,
  output ready,
  output memRead,
  output memWrite,
  output updateAge,
  output readddddd
);

  wire and_2_out, and_3_out, and_4_out, and_5_out, and_6_out, and_7_out, and_8_out, and_9_out, and_10_out,
       and_11_out, and_12_out, and_13_out, and_14_out, and_16_out, and_17_out, not_1_out, not_2_out,
       not_3_out, not_4_out, not_5_out, not_6_out, not_7_out, not_8_out, not_9_out, not_10_out, not_11_out,
       not_12_out, not_13_out, not_14_out, not_15_out, not_16_out, not_17_out, not_18_out, not_19_out,
       not_20_out, not_21_out, not_22_out, not_23_out, not_24_out, not_25_out, not_26_out, not_27_out,
       not_28_out, not_29_out, not_30_out, not_31_out, not_32_out, not_33_out, not_34_out;

  not not_1 (not_1_out, c2);
  not not_2 (not_2_out, c1);
  not not_3 (not_3_out, c0);
  not not_4 (not_4_out, read);
  not not_5 (not_5_out, c0);
  not not_6 (not_6_out, read);
  not not_7 (not_7_out, write);
  not not_8 (not_8_out, c2);
  not not_9 (not_9_out, c1);
  not not_10 (not_10_out, c2);
  not not_11 (not_11_out, c0);
  not not_12 (not_12_out, c0);
  not not_13 (not_13_out, read);
  not not_14 (not_14_out, contain);
  not not_15 (not_15_out, c0);
  not not_16 (not_16_out, write);
  not not_17 (not_17_out, contain);
  not not_18 (not_18_out, c2);
  not not_19 (not_19_out, c0);
  not not_20 (not_20_out, c0);
  not not_21 (not_21_out, read);
  not not_22 (not_22_out, write);
  not not_23 (not_23_out, c0);
  not not_24 (not_24_out, contain);
  not not_25 (not_25_out, dirty);
  not not_26 (not_26_out, c0);
  not not_27 (not_27_out, c1);
  not not_28 (not_28_out, c2);
  not not_29 (not_29_out, c1);
  and and_1 (memRead, c1, c0);
  not not_30 (not_30_out, c2);
  not not_31 (not_31_out, c0);
  not not_32 (not_32_out, c1);
  not not_33 (not_33_out, c0);
  not not_34 (not_34_out, c0);
  and and_2 (and_2_out, not_1_out, c0);
  and and_3 (and_3_out, c2, not_2_out, not_3_out, not_4_out);
  and and_4 (and_4_out, c2, not_5_out, not_6_out, write, contain);
  and and_5 (and_5_out, c2, c1, read, not_7_out, contain);
  and and_6 (and_6_out, not_8_out, not_9_out, c0);
  and and_7 (and_7_out, not_10_out, c1, not_11_out);
  and and_8 (and_8_out, c1, not_12_out, not_13_out, write, not_14_out);
  and and_9 (and_9_out, c1, not_15_out, read, not_16_out, not_17_out);
  and and_10 (and_10_out, not_18_out, not_19_out);
  and and_11 (and_11_out, not_20_out, not_21_out, not_22_out);
  and and_12 (and_12_out, not_23_out, not_24_out, not_25_out);
  and and_13 (and_13_out, not_26_out, read, write);
  and and_14 (and_14_out, c2, not_27_out);
  and and_15 (ready, not_28_out, not_29_out, c0);
  and and_16 (and_16_out, not_30_out, c1, not_31_out);
  and and_17 (and_17_out, c2, c0);
  and and_18 (updateAge, c2, not_32_out, not_33_out);
  and and_19 (readddddd, c2, c1, not_34_out);
  or or_1 (s2, and_2_out, and_3_out, and_4_out, and_5_out);
  or or_2 (s1, and_6_out, and_7_out, and_8_out, and_9_out);
  or or_3 (s0, and_10_out, and_11_out, and_12_out, and_13_out, and_14_out);
  or or_4 (memWrite, and_16_out, and_17_out);
endmodule

module block (
  input  CpuRead,
  input  [7:0] CpuWriteValue,
  input  MemWrite,
  input  [6:0] TAG,
  input  CLK,
  input  dirty,
  input  Read,
  input  [1:0] OS,
  input  Inblock,
  input  InSet,
  input  [31:0] MemRead,
  output Hit,
  output DirtyBit,
  output SetAge0,
  output SetAge0_2,
  output Evict,
  output SetAge0_3,
  output SetAge0_4,
  output SetAge0_5,
  output SetAge0_6,
  output SetAge0_7,
  output SetAge0_8,
  output SetAge0_9,
  output SetAge0_10,
  output SetAge0_11,
  output [6:0] Tag_Out,
  output [7:0] ByteRead,
  output [31:0] LineFromCache
);

  wire and_1_out, and_2_out, and_3_out, and_4_out, and_5_out, and_6_out, and_8_out, and_9_out, and_10_out,
       and_11_out, and_12_out, and_13_out, and_14_out, comparator_1_eq, Dirty0, Dirty0_In, multiplexer_5_out,
       or_1_out, or_2_out, or_3_out, or_4_out, or_5_out, V0, Write_Age0, Write_Dirty0, WriteToReg0,
       WriteToReg1, WriteToReg2, WriteToReg3;
  wire [1:0] Age0, Age0_In;
  wire [7:0] Data0, Data0_In, Data1, Data1_In, Data2, Data2_In, Data3, Data3_In;

  Demultiplexer #(.select(2), .enable("false")) demultiplexer_1 (
    .out0(WriteToReg0), .out1(WriteToReg1), .out2(WriteToReg2), .out3(WriteToReg3), .in(MemWrite), .sel(OS));
  and and_1 (and_1_out, MemWrite, Inblock, InSet, WriteToReg0);
  and and_2 (and_2_out, Inblock, Read, InSet);
  and and_3 (and_3_out, Inblock, InSet);
  and and_4 (and_4_out, Inblock, InSet);
  or or_1 (or_1_out, and_1_out, and_2_out);
  Multiplexer #(.width(8), .enable("false")) multiplexer_1 (
    .in0(MemRead[31:24]), .in1(CpuWriteValue), .out(Data3_In), .sel(MemWrite));
  // Probe on Tag_Out
  Register #(.width(7)) Tag0 (.D(TAG), .en(and_3_out), .Q(Tag_Out), .clk(CLK));  // open: clr
  // Probe on V0
  Register #(.width(1)) u_V0 (.D(1'b1), .en(and_4_out), .Q(V0), .clk(CLK));  // open: clr
  // Probe on Dirty0
  Register #(.width(1)) u_Dirty0 (.D(Dirty0_In), .en(Write_Dirty0), .Q(Dirty0), .clk(CLK));  // open: clr
  // Probe on Age0
  Register #(.width(2)) u_Age0 (.D(Age0_In), .en(Write_Age0), .Q(Age0), .clk(CLK));  // open: clr
  // Probe on Data0
  Register u_Data0 (.D(Data0_In), .en(or_1_out), .Q(Data0), .clk(CLK));  // open: clr
  and and_5 (and_5_out, MemWrite, Inblock, InSet, WriteToReg1);
  and and_6 (and_6_out, Inblock, Read, InSet);
  Multiplexer #(.width(8), .enable("false")) multiplexer_2 (
    .in0(MemRead[23:16]), .in1(CpuWriteValue), .out(Data2_In), .sel(MemWrite));
  or or_2 (or_2_out, and_5_out, and_6_out);
  Multiplexer #(.width(8), .enable("false")) multiplexer_3 (
    .in0(MemRead[7:0]), .in1(CpuWriteValue), .out(Data0_In), .sel(MemWrite));
  // Probe on Data1
  Register Data0_2 (.D(Data1_In), .en(or_2_out), .Q(Data1), .clk(CLK));  // open: clr
  Comparator #(.width(7), .mode("unsigned")) comparator_1 (.a(TAG), .b(Tag_Out), .eq(comparator_1_eq));  // open: gt, lt
  and and_7 (Hit, comparator_1_eq, V0);
  and and_8 (and_8_out, MemWrite, Inblock, InSet, WriteToReg2);
  or or_3 (or_3_out, and_8_out, and_9_out);
  and and_9 (and_9_out, Inblock, Read, InSet);
  Register Data0_3 (.D(Data2_In), .en(or_3_out), .Q(Data2), .clk(CLK));  // open: clr
  Multiplexer #(.width(8), .enable("false")) multiplexer_4 (
    .in0(MemRead[15:8]), .in1(CpuWriteValue), .out(Data1_In), .sel(MemWrite));
  // Probe on Data2
  and and_10 (and_10_out, MemWrite, InSet, Inblock);
  and and_11 (and_11_out, Read, InSet, Inblock);
  and and_12 (and_12_out, InSet, Inblock);
  and and_13 (and_13_out, MemWrite, Inblock, InSet, WriteToReg3);
  and and_14 (and_14_out, Inblock, Read, InSet);
  or or_4 (or_4_out, DirtyBit, and_10_out);
  Multiplexer #(.enable("false")) multiplexer_5 (.in0(or_4_out), .in1(1'b0), .out(multiplexer_5_out), .sel(and_11_out));
  Multiplexer #(.select(2), .width(8), .enable("false")) multiplexer_6 (
    .in0(Data0), .in1(Data1), .in2(Data2), .in3(Data3), .out(ByteRead), .sel(OS));
  Register #(.width(32)) State (
    .D({Data3, Data2, Data1, Data0}), .en(and_12_out), .Q(LineFromCache), .clk(CLK));  // open: clr
  Register Data0_4 (.D(Data3_In), .en(or_5_out), .Q(Data3), .clk(CLK));  // open: clr
  or or_5 (or_5_out, and_13_out, and_14_out);
  D_Flip_Flop d_ff_1 (.clk(CLK), .D(multiplexer_5_out), .Q(DirtyBit));  // open: Qn, preset, en, reset
  and and_15 (Evict, InSet, Read, DirtyBit, Inblock);
  // Probe on Data3

  // Other names for the same wires on the sheet: IsDirtyBit = DirtyBit; LineFromMem[31:0] = MemRead;
  //   Tag0[6:0] = Tag_Out

  // Notes on the sheet:
  //   check if it is in the set
endmodule

module HowOldAmI (
  input  [1:0] Age_1,
  input  [1:0] Age_2,
  input  [1:0] Age_3,
  output [1:0] Grandpa,
  output [1:0] BiggestBoi
);

  wire Age_2_bigger, Age_3_big, comparator_1_gt, comparator_2_gt, comparator_3_gt, comparator_4_gt,
       comparator_5_gt, comparator_6_gt, comparator_7_eq, Oldest_one, Oldest_three, Oldest_two;
  wire [1:0] multiplexer_1_out, multiplexer_2_out, multiplexer_4_out, multiplexer_5_out;

  Comparator #(.width(2), .mode("unsigned")) comparator_1 (.a(Age_1), .b(Age_2), .gt(comparator_1_gt));  // open: eq, lt
  Comparator #(.width(2), .mode("unsigned")) comparator_2 (.a(Age_1), .b(Age_3), .gt(comparator_2_gt));  // open: eq, lt
  Comparator #(.width(2), .mode("unsigned")) comparator_3 (.a(Age_2), .b(Age_1), .gt(comparator_3_gt));  // open: eq, lt
  Comparator #(.width(2), .mode("unsigned")) comparator_4 (.a(Age_2), .b(Age_3), .gt(comparator_4_gt));  // open: eq, lt
  Comparator #(.width(2), .mode("unsigned")) comparator_5 (.a(Age_3), .b(Age_1), .gt(comparator_5_gt));  // open: eq, lt
  Comparator #(.width(2), .mode("unsigned")) comparator_6 (.a(Age_3), .b(Age_2), .gt(comparator_6_gt));  // open: eq, lt
  and and_1 (Oldest_one, comparator_1_gt, comparator_2_gt);
  and and_2 (Oldest_two, comparator_3_gt, comparator_4_gt);
  and and_3 (Oldest_three, comparator_5_gt, comparator_6_gt);
  Multiplexer #(.width(2), .enable("false")) multiplexer_1 (
    .in0(2'b00), .in1(2'b10), .out(multiplexer_1_out), .sel(Age_3_big));
  Multiplexer #(.width(2), .enable("false")) multiplexer_2 (
    .in0(multiplexer_1_out), .in1(2'b01), .out(multiplexer_2_out), .sel(Age_2_bigger));
  Comparator #(.width(1), .mode("unsigned")) comparator_7 (
    .a(Oldest_one), .b(1'b1), .eq(comparator_7_eq));  // open: gt, lt
  Comparator #(.width(1), .mode("unsigned")) comparator_8 (
    .a(Oldest_two), .b(1'b1), .eq(Age_2_bigger));  // open: gt, lt
  Comparator #(.width(1), .mode("unsigned")) comparator_9 (.a(Oldest_three), .b(1'b1), .eq(Age_3_big));  // open: gt, lt
  Multiplexer #(.width(2), .enable("false")) multiplexer_3 (
    .in0(multiplexer_2_out), .in1(2'b00), .out(Grandpa), .sel(comparator_7_eq));
  Multiplexer #(.width(2), .enable("false")) multiplexer_4 (
    .in0(Age_3), .in1(Age_3), .out(multiplexer_4_out), .sel(Age_3_big));
  Multiplexer #(.width(2), .enable("false")) multiplexer_5 (
    .in0(multiplexer_4_out), .in1(Age_2), .out(multiplexer_5_out), .sel(Age_2_bigger));
  Multiplexer #(.width(2), .enable("false")) multiplexer_6 (
    .in0(multiplexer_5_out), .in1(Age_1), .out(BiggestBoi), .sel(comparator_7_eq));
endmodule

module BigBois (
  input  [1:0] Age_0,
  input  [1:0] Age_1,
  input  [1:0] Age_2,
  input  [1:0] BIGBOI,
  input  A1,
  input  A2,
  input  A3,
  output [1:0] New_Age0,
  output [1:0] New_Age1,
  output [1:0] New_Age2
);

  wire comparator_1_lt, comparator_2_lt, comparator_3_eq, comparator_4_eq, comparator_5_lt, comparator_6_eq;
  wire [1:0] adder_1_out, adder_2_out, adder_3_out, BB, multiplexer_1_out, multiplexer_2_out,
       multiplexer_6_out;

  Adder #(.width(2)) adder_1 (.a(2'b01), .b(Age_0), .out(adder_1_out));  // open: cin, cout
  Adder #(.width(2)) adder_2 (.a(2'b01), .b(Age_1), .out(adder_2_out));  // open: cin, cout
  Comparator #(.width(2), .mode("unsigned")) comparator_1 (.a(Age_1), .b(BB), .lt(comparator_1_lt));  // open: gt, eq
  Multiplexer #(.width(2), .enable("false")) multiplexer_1 (
    .in0(Age_0), .in1(adder_1_out), .out(multiplexer_1_out), .sel(comparator_2_lt));
  Comparator #(.width(2), .mode("unsigned")) comparator_2 (.a(Age_0), .b(BB), .lt(comparator_2_lt));  // open: gt, eq
  Comparator #(.width(2), .mode("unsigned")) comparator_3 (.a(Age_0), .b(BB), .eq(comparator_3_eq));  // open: gt, lt
  Multiplexer #(.width(2), .enable("false")) multiplexer_2 (
    .in0(Age_1), .in1(adder_2_out), .out(multiplexer_2_out), .sel(comparator_1_lt));
  Comparator #(.width(2), .mode("unsigned")) comparator_4 (.a(Age_1), .b(BB), .eq(comparator_4_eq));  // open: gt, lt
  Multiplexer #(.width(2), .enable("false")) multiplexer_3 (
    .in0(multiplexer_2_out), .in1(2'b00), .out(New_Age1), .sel(comparator_4_eq));
  Multiplexer #(.select(3), .width(2), .enable("false")) multiplexer_4 (
    .in1(Age_0), .in2(Age_1), .in4(Age_2), .out(BB), .sel({A3, A2, A1}));  // open: in0, in3, in5, in6, in7
  Multiplexer #(.width(2), .enable("false")) multiplexer_5 (
    .in0(multiplexer_1_out), .in1(2'b00), .out(New_Age0), .sel(comparator_3_eq));
  Adder #(.width(2)) adder_3 (.a(2'b01), .b(Age_2), .out(adder_3_out));  // open: cin, cout
  Comparator #(.width(2), .mode("unsigned")) comparator_5 (.a(Age_2), .b(BB), .lt(comparator_5_lt));  // open: gt, eq
  Multiplexer #(.width(2), .enable("false")) multiplexer_6 (
    .in0(Age_2), .in1(adder_3_out), .out(multiplexer_6_out), .sel(comparator_5_lt));
  Comparator #(.width(2), .mode("unsigned")) comparator_6 (.a(Age_2), .b(BB), .eq(comparator_6_eq));  // open: gt, lt
  Multiplexer #(.width(2), .enable("false")) multiplexer_7 (
    .in0(multiplexer_6_out), .in1(2'b00), .out(New_Age2), .sel(comparator_6_eq));

  // Other names for the same wires on the sheet: Age0[1:0] = Age_0; Age1[1:0] = Age_1; Age2[1:0] = Age_2;
  //   BB_FAKE[1:0] = BIGBOI; Path[2:0] = {A3, A2, A1}
endmodule
