// Logisim project Shift3.circ as structural Verilog: 4 circuits, main circuit main
module main (
  input  Enable_Halt
);

  wire and_2_out, CLK, Correct, Do_Right_Shift, Halt, not_1_out, not_2_out, NotDone;
  wire [1:0] Shift_Amount;
  wire [2:0] Correct_Answer, Num, Your_Answer;
  wire [6:0] counter_1_q;

  not not_1 (not_1_out, Correct);
  and and_1 (Halt, Enable_Halt, not_1_out);
  Inputs inputs_1 (
    .Halt(Halt), .CLK(CLK), .Do_Right_Shift(Do_Right_Shift), .ShiftAmount(Shift_Amount), .Num(Num),
    .NotDone(NotDone));
  Clock clock_1 (.out(CLK));
  // Probe on Do_Right_Shift
  // Probe on Shift_Amount
  // Probe on Num
  // Probe on Your_Answer
  // Probe on Correct_Answer
  Shifter3 shifter3_1 (
    .Num(Num), .Shift_amount(Shift_Amount), .Do_Right_Shift(Do_Right_Shift), .Shifted_Num(Your_Answer));
  not not_2 (not_2_out, Halt);
  and and_2 (and_2_out, Correct, NotDone, not_2_out);
  Checker checker_1 (
    .Do_Right_Shift(Do_Right_Shift), .Shift_Amount(Shift_Amount), .Num(Num), .Shifted_Num(Your_Answer),
    .Correct(Correct), .Correct_Num(Correct_Answer));
  Counter #(.width(7), .max('h40)) counter_1 (
    .count(and_2_out), .Q(counter_1_q), .clk(CLK));  // open: load, D, carry, clr
  // Probe on counter_1_q

  // Notes on the sheet:
  //   Use the Poke Tool on the enable halt input to enable/disable halting
  //   Enabling Halt will cause the testing to stop as soon as the first incorrect answer is detected
  //   Armand Nasseri  912679383
  //   Stephanie Dennis 913392339 
endmodule

module Shifter3 (
  input  [2:0] Num,
  input  [1:0] Shift_amount,
  input  Do_Right_Shift,
  output [2:0] Shifted_Num
);

  wire multiplexer_1_out, multiplexer_2_out, multiplexer_3_out, multiplexer_4_out, multiplexer_5_out,
       multiplexer_6_out;

  Multiplexer #(.select(2)) multiplexer_1 (
    .in0(Num[2]), .in1(Num[1]), .in2(Num[0]), .in3(1'b0), .out(multiplexer_1_out), .sel(Shift_amount));  // open: en
  Multiplexer #(.select(2)) multiplexer_2 (
    .in0(Num[1]), .in1(Num[0]), .in2(1'b0), .in3(1'b0), .out(multiplexer_2_out), .sel(Shift_amount));  // open: en
  Multiplexer #(.select(2)) multiplexer_3 (
    .in0(Num[0]), .in1(1'b0), .in2(1'b0), .in3(1'b0), .out(multiplexer_3_out), .sel(Shift_amount));  // open: en
  Multiplexer #(.select(2)) multiplexer_4 (
    .in0(Num[2]), .in1(1'b0), .in2(1'b0), .in3(1'b0), .out(multiplexer_4_out), .sel(Shift_amount));  // open: en
  Multiplexer #(.select(2)) multiplexer_5 (
    .in0(Num[1]), .in1(Num[2]), .in2(1'b0), .in3(1'b0), .out(multiplexer_5_out), .sel(Shift_amount));  // open: en
  Multiplexer #(.select(2)) multiplexer_6 (
    .in0(Num[0]), .in1(Num[1]), .in2(Num[2]), .in3(1'b0), .out(multiplexer_6_out), .sel(Shift_amount));  // open: en
  Multiplexer multiplexer_7 (
    .in0(multiplexer_1_out), .in1(multiplexer_4_out), .out(Shifted_Num[2]), .sel(Do_Right_Shift));  // open: en
  Multiplexer multiplexer_8 (
    .in0(multiplexer_2_out), .in1(multiplexer_5_out), .out(Shifted_Num[1]), .sel(Do_Right_Shift));  // open: en
  Multiplexer multiplexer_9 (
    .in0(multiplexer_3_out), .in1(multiplexer_6_out), .out(Shifted_Num[0]), .sel(Do_Right_Shift));  // open: en

  // Notes on the sheet:
  //   Left Shift
  //   Right Shift
endmodule

module Inputs (
  input  Halt,
  input  CLK,
  output Do_Right_Shift,
  output [1:0] ShiftAmount,
  output [2:0] Num,
  output NotDone
);

  wire counter_1_carry, nHalt, register_1_q;

  not not_1 (nHalt, Halt);
  Counter #(.width(6), .max('h3f), .ongoal("stay")) counter_1 (
    .count(nHalt), .Q({Do_Right_Shift, ShiftAmount, Num}), .carry(counter_1_carry), .clk(CLK));  // open: load, D, clr
  not not_2 (NotDone, register_1_q);
  Register #(.width(1)) register_1 (.D(counter_1_carry), .en(NotDone), .Q(register_1_q), .clk(CLK));  // open: clr
endmodule

module Checker (
  input  Do_Right_Shift,
  input  [1:0] Shift_Amount,
  input  [2:0] Num,
  input  [2:0] Shifted_Num,
  output Correct,
  output [2:0] Correct_Num
);

  ROM #(.addrWidth(6), .dataWidth(3)) rom_1 (
    .addr({Do_Right_Shift, Shift_Amount, Num}), .data(Correct_Num));  // open: sel
  Comparator #(.width(3)) comparator_1 (.a(Correct_Num), .b(Shifted_Num), .eq(Correct));  // open: gt, lt

  // Notes on the sheet:
  //   contents of rom_1 (hex, n*v repeats v):
  //   0 1 2 3 4 5 6 7 0 2 4 6 0 2 4 6 0 4 0 4 0 4 0 4 9*0 1 2 3 4 5 6 7 0 0 1 1 2 2 3 3 4*0 4*1
endmodule
