// Logisim project 4BitParity.circ as structural Verilog: 4 circuits, main circuit main
module main (
  input  Halt_Enable
);

  wire and_2_out, CLK, Correct, Done_Testing, Halt, Input, not_1_out, not_2_out, not_3_out, Solution,
       YourAnswer;
  wire [6:0] counter_1_q, TestNumber;

  not not_1 (not_1_out, Correct);
  Clock clock_1 (.out(CLK));
  and and_1 (Halt, Halt_Enable, not_1_out);
  Inputs inputs_1 (.Halt(Halt), .CLK(CLK), .Input(Input), .TestNumber(TestNumber), .Done_Testing(Done_Testing));
  _4BitEvenParity u_4bitevenparity_1 (.Input(Input), .CLK(CLK), .Is_Even(YourAnswer));
  // Probe on Input
  // Probe on YourAnswer
  // Probe on Solution
  // Probe on Correct
  not not_2 (not_2_out, Halt);
  and and_2 (and_2_out, Correct, not_2_out, not_3_out);
  not not_3 (not_3_out, Done_Testing);
  Checker checker_1 (.Your_Answer(YourAnswer), .TestNumber(TestNumber), .Correct(Correct), .Solution(Solution));
  Counter #(.width(7), .max('h41), .ongoal("stay")) counter_1 (
    .count(and_2_out), .Q(counter_1_q), .clk(CLK));  // open: load, D, carry, clr
  // Probe on counter_1_q

  // Notes on the sheet:
  //   Armand Nasseri    912679383
  //   Max 65
endmodule

module _4BitEvenParity (
  input  Input,
  input  CLK,
  output Is_Even
);

  wire and_1_out, and_2_out, and_3_out, and_4_out, and_5_out, and_6_out, and_7_out, and_8_out, d_ff_1_q,
       d_ff_3_q, d_ff_4_q, not_1_out, not_2_out, not_3_out, not_4_out, not_5_out, or_1_out, or_2_out,
       or_3_out, or_4_out, or_5_out, or_6_out, or_7_out, or_8_out, or_9_out, or_10_out, s2;

  not not_1 (not_1_out, Input);
  not not_2 (not_2_out, d_ff_4_q);
  not not_3 (not_3_out, d_ff_3_q);
  not not_4 (not_4_out, s2);
  not not_5 (not_5_out, d_ff_1_q);
  and and_1 (and_1_out, d_ff_3_q, not_5_out);
  and and_2 (and_2_out, not_1_out, d_ff_4_q, not_5_out, not_4_out);
  or or_1 (or_1_out, Input, not_2_out, d_ff_1_q, not_4_out);
  or or_2 (or_2_out, not_1_out, d_ff_4_q, s2);
  or or_3 (or_3_out, not_1_out, d_ff_3_q, not_4_out, not_5_out);
  or or_4 (or_4_out, not_1_out, not_3_out, not_2_out, not_5_out);
  or or_5 (or_5_out, not_1_out, not_3_out, d_ff_1_q, s2);
  and and_3 (and_3_out, d_ff_3_q, not_5_out);
  and and_4 (and_4_out, d_ff_4_q, s2, not_5_out);
  and and_5 (and_5_out, not_3_out, d_ff_1_q);
  or or_6 (or_6_out, not_1_out, d_ff_4_q, d_ff_1_q, not_4_out);
  or or_7 (or_7_out, Input, not_2_out, not_5_out);
  or or_8 (or_8_out, Input, d_ff_3_q, s2);
  or or_9 (or_9_out, and_1_out, and_6_out, and_2_out);
  or or_10 (or_10_out, and_3_out, and_4_out, and_5_out);
  D_Flip_Flop d_ff_1 (.clk(CLK), .D(or_9_out), .Q(d_ff_1_q));  // open: Qn, preset, en, reset
  and and_6 (and_6_out, Input, not_3_out, not_2_out, not_5_out, s2);
  and and_7 (and_7_out, or_1_out, or_2_out, or_3_out, or_4_out, or_5_out);
  and and_8 (and_8_out, or_6_out, or_7_out, or_8_out);
  D_Flip_Flop d_ff_2 (.clk(CLK), .D(and_7_out), .Q(s2));  // open: Qn, preset, en, reset
  D_Flip_Flop d_ff_3 (.clk(CLK), .D(or_10_out), .Q(d_ff_3_q));  // open: Qn, preset, en, reset
  D_Flip_Flop d_ff_4 (.clk(CLK), .D(and_8_out), .Q(d_ff_4_q));  // open: Qn, preset, en, reset
  and and_9 (Is_Even, d_ff_1_q, s2, d_ff_3_q);

  // Notes on the sheet:
  //   s0
  //   s1
  //   s3
  //   s2
  //   s3
  //   s2
  //   s0
  //   s1
endmodule

module Inputs (
  input  Halt,
  input  CLK,
  output Input,
  output [6:0] TestNumber,
  output Done_Testing
);

  wire not_1_out;

  not not_1 (not_1_out, Halt);
  Counter #(.width(7), .max('h41), .ongoal("stay")) counter_1 (
    .count(not_1_out), .Q(TestNumber), .carry(Done_Testing), .clk(CLK));  // open: load, D, clr
  ROM #(.addrWidth(7), .dataWidth(1)) rom_1 (.addr(TestNumber), .data(Input));  // open: sel

  // Notes on the sheet:
  //   contents of rom_1 (hex, n*v repeats v):
  //   7*0 1 0 0 1 0 0 0 1 1 0 1 0 0 0 1 0 1 0 1 1 0 0 4*1 0 0 0 1 0 0 1 1 0 1 0 1 0 4*1 0 0 1 1 0 4*1 0
  //   4*1
endmodule

module Checker (
  input  Your_Answer,
  input  [6:0] TestNumber,
  output Correct,
  output Solution
);

  ROM #(.addrWidth(7), .dataWidth(1)) rom_1 (.addr(TestNumber), .data(Solution));  // open: sel
  Comparator #(.width(1)) comparator_1 (.a(Solution), .b(Your_Answer), .eq(Correct));  // open: gt, lt

  // Notes on the sheet:
  //   contents of rom_1 (hex, n*v repeats v):
  //   4*0 1 11*0 1 7*0 1 0 0 0 1 11*0 1 0 0 0 1 7*0 1 11*0 1
endmodule
